# Fritzing sketch pico-rotate (saved by Fritzing 1.0.1rc)
circuit board: 7.12582cm x 4.92247cm
breadboards: 1

parts:
  LCM1602_IIC1 = LCM1602 IIC [part_number="LCM1602 IIC" chip_label="LCM1602 IIC" package="DIP (Dual Inline) [THT]"]
  Pico_H1 = Raspberry Pi Pico H
  MOTOR1 = 28BYJ-48 Stepper Motor
  Driver1 = 28BYJ-48 Driver Module [part_number=ULN2003 package=THT]
  S1 = Pushbutton [package="[SMD]"]
  S2 = Pushbutton [package="[SMD]"]
  S3 = Pushbutton [package="[SMD]"]
  S4 = Pushbutton [package="[SMD]"]
  U1 = SWITCH_SPDT [package=kps-1290]

nets:
  GND: LCM1602_IIC1.GND, Pico_H1.GND, Driver1.GND, S1.Pin_3, S1.Pin_4, S2.Pin_3, S2.Pin_4, S3.Pin_3, S3.Pin_4, S4.Pin_3, S4.Pin_4
  N1: LCM1602_IIC1.VCC, Pico_H1.VSYS, Driver1.Vmotor, U1.S
  N2: LCM1602_IIC1.SDA, Pico_H1.GP2
  N3: LCM1602_IIC1.SCL, Pico_H1.GP3
  N4: Pico_H1.GP21, Driver1.IN4
  N5: Pico_H1.GP20, Driver1.IN3
  N6: Pico_H1.GP19, Driver1.IN2
  N7: Pico_H1.GP18, Driver1.IN1
  N8: Pico_H1.GP15, S4.Pin_1, S4.Pin_2
  N9: Pico_H1.GP14, S2.Pin_1, S2.Pin_2
  N10: Pico_H1.GP13, S3.Pin_1, S3.Pin_2
  N11: Pico_H1.GP12, S1.Pin_1, S1.Pin_2
  N12: MOTOR1.RED, Driver1.red-pin
  N13: MOTOR1.ORANGE, Driver1.orange-pin
  N14: MOTOR1.YELLOW, Driver1.yellow-pin
  N15: MOTOR1.PINK, Driver1.pink-pin
  N16: MOTOR1.BLUE, Driver1.blue-pin

custom parts:
  LCM1602 IIC: I2C-Module to use a 1602 or 2004 LCD on with the wire.h libory Serial LCD Modul
  Raspberry Pi Pico H: Raspberry Pi Pico H. Based around the RP2040 microcontroller the Pico H is a low cost microcontroller device bringing Raspberry Pi quality, cost, and easy of use to the microcontroller space.
  28BYJ-48 Driver Module: ULN2003 Driver Module for the 28BYJ-48 Unipolar Stepper Motor LED A - Blue wire - Bottom coil left LED B - Pink wire - Top coil left LED C - Yellow wire - Bottom coil right LED D - Orange wire - Top coil right Common rail - red Connector pins: blue - pink - yellow - orange - red Control pins - IN1 to IN4 Power pins - GND & Vmotor (5-12V) On/Off jumper (if removed, power to motor is cut).
